# Fritzing sketch fritzing (saved by Fritzing 0.9.3b)
breadboards: 1

parts:
  Raspberry_Pi_1 = Raspberry Pi B+
  LED1 = smd LED [color="Red (633nm)" package="1206 [SMD]"]
  R1 = Resistor [tolerance=±5% resistance=220 package="0402 [SMD]"]

nets:
  N1: Raspberry_Pi_1.3V3, Raspberry_Pi_1.GPIO24, LED1.cathode
  N2: Raspberry_Pi_1.GPIO5, Raspberry_Pi_1.GND, R1.Pin_1
  N3: LED1.anode, R1.Pin_0
